// Logisim project Registradores.circ as structural Verilog: 1 circuit, main circuit main
module main (
);

  wire clock_1_out, demultiplexer_1_out0, demultiplexer_1_out1, demultiplexer_1_out2, demultiplexer_1_out3,
       demultiplexer_1_out4, demultiplexer_1_out5, demultiplexer_1_out6, demultiplexer_1_out7;
  wire [31:0] multiplexer_1_out, register_1_q, register_5_q, register_9_q, register_13_q, register_14_q,
       register_21_q, register_25_q, register_29_q;

  Demultiplexer #(.select(5)) demultiplexer_1 (
    .out0(demultiplexer_1_out0), .out1(demultiplexer_1_out1), .out2(demultiplexer_1_out2),
    .out3(demultiplexer_1_out3), .out4(demultiplexer_1_out4), .out5(demultiplexer_1_out5),
    .out6(demultiplexer_1_out6), .out7(demultiplexer_1_out7), .in(1'b1), .sel(5'b00011));  // open: out8, out9, out10, out11, out12, out13, out14, out15, out16, out17, out18, out19, out20, out21, out22, out23, out24, out25, out26, out27, out28, out29, out30, out31, en
  Clock clock_1 (.out(clock_1_out));
  Register #(.width(32)) register_1 (
    .D(32'h2211), .en(demultiplexer_1_out7), .Q(register_1_q), .clk(clock_1_out));  // open: clr
  Register #(.width(32)) register_2 (.D(32'h2211), .clk(clock_1_out));  // open: en, Q, clr
  Register #(.width(32)) register_3 (.D(32'h2211), .clk(clock_1_out));  // open: en, Q, clr
  Register #(.width(32)) register_4 (.D(32'h2211), .clk(clock_1_out));  // open: en, Q, clr
  Register #(.width(32)) register_5 (
    .D(32'h2211), .en(demultiplexer_1_out6), .Q(register_5_q), .clk(clock_1_out));  // open: clr
  Register #(.width(32)) register_6 (.D(32'h2211), .clk(clock_1_out));  // open: en, Q, clr
  Register #(.width(32)) register_7 (.D(32'h2211), .clk(clock_1_out));  // open: en, Q, clr
  Register #(.width(32)) register_8 (.D(32'h2211), .clk(clock_1_out));  // open: en, Q, clr
  Register #(.width(32)) register_9 (
    .D(32'h2211), .en(demultiplexer_1_out5), .Q(register_9_q), .clk(clock_1_out));  // open: clr
  Register #(.width(32)) register_10 (.D(32'h2211), .clk(clock_1_out));  // open: en, Q, clr
  Register #(.width(32)) register_11 (.D(32'h2211), .clk(clock_1_out));  // open: en, Q, clr
  Register #(.width(32)) register_12 (.D(32'h2211), .clk(clock_1_out));  // open: en, Q, clr
  Register #(.width(32)) register_13 (
    .D(32'h2211), .en(demultiplexer_1_out4), .Q(register_13_q), .clk(clock_1_out));  // open: clr
  Register #(.width(32)) register_14 (
    .D(32'h2211), .en(demultiplexer_1_out3), .Q(register_14_q), .clk(clock_1_out));  // open: clr
  Register #(.width(32)) register_15 (.D(32'h2211), .clk(clock_1_out));  // open: en, Q, clr
  Register #(.width(32)) register_16 (.D(32'h2211), .clk(clock_1_out));  // open: en, Q, clr
  Register #(.width(32)) register_17 (.D(32'h2211), .clk(clock_1_out));  // open: en, Q, clr
  Register #(.width(32)) register_18 (.D(32'h2211), .clk(clock_1_out));  // open: en, Q, clr
  Register #(.width(32)) register_19 (.D(32'h2211), .clk(clock_1_out));  // open: en, Q, clr
  Register #(.width(32)) register_20 (.D(32'h2211), .clk(clock_1_out));  // open: en, Q, clr
  Register #(.width(32)) register_21 (
    .D(32'h2211), .en(demultiplexer_1_out2), .Q(register_21_q), .clk(clock_1_out));  // open: clr
  Register #(.width(32)) register_22 (.D(32'h2211), .clk(clock_1_out));  // open: en, Q, clr
  Register #(.width(32)) register_23 (.D(32'h2211), .clk(clock_1_out));  // open: en, Q, clr
  Register #(.width(32)) register_24 (.D(32'h2211), .clk(clock_1_out));  // open: en, Q, clr
  Register #(.width(32)) register_25 (
    .D(32'h2211), .en(demultiplexer_1_out1), .Q(register_25_q), .clk(clock_1_out));  // open: clr
  Register #(.width(32)) register_26 (.D(32'h2211), .clk(clock_1_out));  // open: en, Q, clr
  Register #(.width(32)) register_27 (.D(32'h2211), .clk(clock_1_out));  // open: en, Q, clr
  Register #(.width(32)) register_28 (.D(32'h2211), .clk(clock_1_out));  // open: en, Q, clr
  Register #(.width(32)) register_29 (
    .D(32'h2211), .en(demultiplexer_1_out0), .Q(register_29_q), .clk(clock_1_out));  // open: clr
  Register #(.width(32)) register_30 (.D(32'h2211), .clk(clock_1_out));  // open: en, Q, clr
  Register #(.width(32)) register_31 (.D(32'h2211), .clk(clock_1_out));  // open: en, Q, clr
  Register #(.width(32)) register_32 (.D(32'h2211), .clk(clock_1_out));  // open: en, Q, clr
  Multiplexer #(.select(5), .width(32)) multiplexer_1 (
    .in0(register_1_q), .in1(register_5_q), .in2(register_9_q), .in3(register_13_q), .in4(register_14_q),
    .in5(register_21_q), .in6(register_25_q), .in7(register_29_q), .out(multiplexer_1_out), .sel(5'b00100));  // open: in8, in9, in10, in11, in12, in13, in14, in15, in16, in17, in18, in19, in20, in21, in22, in23, in24, in25, in26, in27, in28, in29, in30, in31, en
  // Probe on multiplexer_1_out
endmodule
